# Fritzing sketch KiteReleasePayload (saved by Fritzing 1.0.5)
circuit board: 3.6cm x 3.60379cm

parts:
  J1 = Dagu DGServo 9g header connector (female) [package=THT]
  JP1 = Header 2 [package=screwterminal-3.5mm-2_lock]
  J2 = female pin header, 2 pins [form="♀ (female)"]
  J3 = female pin header, 2 pins [form="♀ (female)"]
  WeMos_D1_Mini1 = WeMos D1 Mini

nets:
  N1: J1.gnd, JP1.2, J3.pin2, WeMos_D1_Mini1.G
  VCC: J1.Vcc, JP1.1, WeMos_D1_Mini1.5V
  N2: J1.pulse, WeMos_D1_Mini1.D5
  N3: J2.pin1, WeMos_D1_Mini1.D1
  N4: J2.pin2, WeMos_D1_Mini1.D2
  N5: J3.pin1, WeMos_D1_Mini1.3V3
